// Logisim project LabArqui.circ as structural Verilog
module OneBitComparator (
  input  A,
  input  B,
  output AGB,
  output ALB,
  output AEB
);

  wire not_1_out, not_2_out, or_1_out;

  not not_1 (not_1_out, B);
  not not_2 (not_2_out, A);
  and and_1 (AGB, A, not_1_out);
  and and_2 (ALB, not_2_out, B);
  or or_1 (or_1_out, ALB, AGB);
  not not_3 (AEB, or_1_out);

  // Notes on the sheet:
  //   A>B
  //   A<B
  //   A=B
endmodule

module EightBitComparator (
  input  A7,
  input  A6,
  input  A5,
  input  A4,
  input  A3,
  input  A2,
  input  A1,
  input  A0,
  input  B7,
  input  B6,
  input  B5,
  input  B4,
  input  B3,
  input  B2,
  input  B1,
  input  B0,
  output AGB,
  output ALB,
  output AEB
);

  wire and_1_out, and_2_out, fourbitcomparator_1_aeb, fourbitcomparator_1_agb, fourbitcomparator_1_alb,
       fourbitcomparator_2_aeb, fourbitcomparator_2_agb, fourbitcomparator_2_alb;

  FourBitComparator fourbitcomparator_1 (
    .A3(A7), .A2(A6), .B3(B7), .B2(B6), .A1(A5), .A0(A4), .B1(B5), .B0(B4), .AGB(fourbitcomparator_1_agb),
    .ALB(fourbitcomparator_1_alb), .AEB(fourbitcomparator_1_aeb));
  FourBitComparator fourbitcomparator_2 (
    .A3(A3), .A2(A2), .B3(B3), .B2(B2), .A1(A1), .A0(A0), .B1(B1), .B0(B0), .AGB(fourbitcomparator_2_agb),
    .ALB(fourbitcomparator_2_alb), .AEB(fourbitcomparator_2_aeb));
  and and_1 (and_1_out, fourbitcomparator_1_aeb, fourbitcomparator_2_agb);
  and and_2 (and_2_out, fourbitcomparator_1_aeb, fourbitcomparator_2_alb);
  or or_1 (AGB, fourbitcomparator_1_agb, and_1_out);
  or or_2 (ALB, fourbitcomparator_1_alb, and_2_out);
  and and_3 (AEB, fourbitcomparator_1_aeb, fourbitcomparator_2_aeb);
endmodule

module TwoBitComparator (
  input  A1,
  input  A0,
  input  B1,
  input  B0,
  output AGB,
  output ALB,
  output AEB
);

  wire and_1_out, and_2_out, onebitcomparator_1_aeb, onebitcomparator_1_agb, onebitcomparator_1_alb,
       onebitcomparator_2_aeb, onebitcomparator_2_agb, onebitcomparator_2_alb;

  OneBitComparator onebitcomparator_1 (
    .A(A1), .B(B1), .AGB(onebitcomparator_1_agb), .ALB(onebitcomparator_1_alb), .AEB(onebitcomparator_1_aeb));
  OneBitComparator onebitcomparator_2 (
    .A(A0), .B(B0), .AGB(onebitcomparator_2_agb), .ALB(onebitcomparator_2_alb), .AEB(onebitcomparator_2_aeb));
  and and_1 (and_1_out, onebitcomparator_1_aeb, onebitcomparator_2_agb);
  and and_2 (and_2_out, onebitcomparator_2_alb, onebitcomparator_1_aeb);
  or or_1 (AGB, onebitcomparator_1_agb, and_1_out);
  or or_2 (ALB, onebitcomparator_1_alb, and_2_out);
  and and_3 (AEB, onebitcomparator_1_aeb, onebitcomparator_2_aeb);

  // Notes on the sheet:
  //   +SBIT
  //   -SBIT
endmodule

module FourBitComparator (
  input  A3,
  input  A2,
  input  B3,
  input  B2,
  input  A1,
  input  A0,
  input  B1,
  input  B0,
  output AGB,
  output ALB,
  output AEB
);

  wire and_1_out, and_2_out, twobitcomparator_1_aeb, twobitcomparator_1_agb, twobitcomparator_1_alb,
       twobitcomparator_2_aeb, twobitcomparator_2_agb, twobitcomparator_2_alb;

  TwoBitComparator twobitcomparator_1 (
    .A1(A3), .A0(A2), .B1(B3), .B0(B2), .AGB(twobitcomparator_1_agb), .ALB(twobitcomparator_1_alb),
    .AEB(twobitcomparator_1_aeb));
  TwoBitComparator twobitcomparator_2 (
    .A1(A1), .A0(A0), .B1(B1), .B0(B0), .AGB(twobitcomparator_2_agb), .ALB(twobitcomparator_2_alb),
    .AEB(twobitcomparator_2_aeb));
  and and_1 (and_1_out, twobitcomparator_1_aeb, twobitcomparator_2_agb);
  and and_2 (and_2_out, twobitcomparator_2_alb, twobitcomparator_1_aeb);
  or or_1 (AGB, twobitcomparator_1_agb, and_1_out);
  or or_2 (ALB, twobitcomparator_1_alb, and_2_out);
  and and_3 (AEB, twobitcomparator_1_aeb, twobitcomparator_2_aeb);

  // Notes on the sheet:
  //   +SBIT
  //   -SBIT
endmodule
